# Fritzing sketch Gameboy (saved by Fritzing 0.9.3b)
perfboards: 1

parts:
  U1 = NodeMCU V3.0
  U3 = JOYSTICK-PSP1000 [package=joystick-psp1000]
  Q1 = NPN-Transistor [package="TO92 [THT]"]
  Q2 = NPN-Transistor [package="TO92 [THT]"]
  R1 = Resistor [tolerance=±5% resistance=2.2k package=THT]
  R2 = Resistor [tolerance=±5% resistance=2.2k package=THT]
  S1 = Pushbutton [package="[THT]"]
  S2 = Pushbutton [package="[THT]"]
  S3 = Pushbutton [package="[THT]"]
  Part1 = TFT 1.8 inch 160x128 w microSD [part_number=358]
  U4 = BATTERY-2 [package=battery-aa]

nets:
  N1: U1.D2, S1.Pin_3, S1.Pin_4
  N2: U1.D4, S2.Pin_3, S2.Pin_4
  3V3: U1.3V3, U3.VCC, S3.Pin_1, S3.Pin_2, Part1.LITE, Part1.+5V
  GND: U1.GND#6, U1.GND#13, U1.GND#16, U1.GND#33, U3.GND, S1.Pin_1, S1.Pin_2, S2.Pin_1, S2.Pin_2, Part1.GND, U4.-1
  N3: U1.D5, Part1.SCLK
  N4: U1.D6, Part1.TFTDC
  N5: U1.D7, Part1.MOSI
  N6: U1.RST, Part1.RESET
  N7: U1.S2, R2.Pin_0
  N8: U1.S3, R1.Pin_0
  N9: U1.A0, Q1.E, Q2.E
  N10: U3.X, Q1.C
  N11: U3.Y, Q2.C
  N12: Q1.B, R2.Pin_1
  N13: Q2.B, R1.Pin_1
  N14: S3.Pin_3, S3.Pin_4, U4.+1

custom parts:
  NodeMCU V3.0: ESP8266 based NodeMCU
  TFT 1.8 inch 160x128 w microSD: This lovely little display breakout is the best way to add a small, colorful and bright display to any project. Since the display uses 4-wire SPI to communicate and has its own pixel-addressable frame buffer, it can be used with every kind of microcontroller. Even a very small one with low memory and few pins available! The 1.8" display has 128x160 color pixels.
